# Fritzing sketch Pi Hat (saved by Fritzing 0.9.4)
circuit board: 6.47278cm x 4.89617cm

parts:
  Part1 = Adafruit TB6612 DC and Stepper Motor Driver [part_number="Adafruit #2448"]
  J1 = screw terminal, 4 pins
  PWR_IN = Screw terminal - 2 pins [package=THT]
  U1 = Voltage Regulator - 5V [package="TO220 [THT]"]
  STOP = female pin header, 2 pins [form="♀ (female)"]
  MCU1 = Raspberry Pi Zero
  PWR_SWT = female pin header, 2 pins [form="♀ (female)"]
  +_RGB = female pin header, 3 pins [form="♀ (female)"]
  Level_Shifter = Adafruit 4-channel I2C-safe Bi-directional Logic Level Converter [part_number="Adafruit #757"]

nets:
  N1: Part1.PWRIN, U1.input_voltage, PWR_SWT.pin1
  N2: Part1.VCC, Part1.PWMB, Part1.PWMA, MCU1.pin_17, Level_Shifter.LV
  GND: Part1.GND, PWR_IN.pin2, U1.GND, STOP.pin2, MCU1.pin_6, MCU1.pin_9, MCU1.pin_34, MCU1.pin_39, +_RGB.pin3, Level_Shifter.GND
  N3: Part1.BIN2, MCU1.pin_37
  N4: Part1.BIN1, MCU1.pin_35
  N5: Part1.STBY, STOP.pin1, MCU1.pin_33
  N6: Part1.AIN1, MCU1.pin_31
  N7: Part1.AIN2, MCU1.pin_29
  N8: Part1.MOTORA1, J1.pin2
  N9: Part1.MOTORA2, J1.pin1
  N10: Part1.MOTORB2, J1.pin3
  N11: Part1.MOTORB1, J1.pin4
  N12: PWR_IN.pin1, PWR_SWT.pin2
  N13: U1.output_voltage, MCU1.pin_2, MCU1.pin_4, +_RGB.pin1, Level_Shifter.HV
  N14: MCU1.pin_18, Level_Shifter.A1
  N15: +_RGB.pin2, Level_Shifter.B1

notes:
  M1
  M2
  AIN2 <-> GPIO5
  AIN1 <-> GPIO6
  STBY <-> GPIO13
  BIN1 <-> GPIO19
  BIN2 <-> GPIO26
  PiBot Control Board v1
  Designed by J M Sams

custom parts:
  Adafruit TB6612 DC and Stepper Motor Driver: Spin two DC motors, step one bi-polar or uni-polar stepper, or fire off two solenoids with 1.2A per channel using the TB6612. These are perhaps better known as "the drivers in our assembled Adafruit Motorshield or Motor HAT." We really like these dual H-bridges, so if you want to control motors without a shield or HAT these are easy to include on any solderless breadboard or perma-proto.
  Adafruit 4-channel I2C-safe Bi-directional Logic Level Converter: Because the Arduino (and Basic Stamp) are 5V devices, and most modern sensors, displays, flash cards and modes are 3.3V-only, many makers find that they need to perform level shifting/conversion to protect the 3.3V device from 5V. We do have some other handy level shifters in the shop, from the DIP 74LVC245 to the fancy bi-directional TXB0108. However, neither of these are happy to work with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
